# Fritzing sketch arcadeduino (saved by Fritzing 0.9.2b)
circuit board: 7.68887cm x 5.59171cm
breadboards: 2

parts:
  Part1 = Arduino Uno (Rev3)
  R1 = Resistor [tolerance=±5% resistance=470 package=THT]
  R2 = Resistor [tolerance=±5% resistance=470 package=THT]
  R3 = Resistor [tolerance=±5% resistance=470 package=THT]
  R4 = Resistor [tolerance=±5% resistance=470 package=THT]
  R5 = Resistor [tolerance=±5% resistance=470 package=THT]
  R6 = Resistor [tolerance=±5% resistance=470 package=THT]
  R7 = Resistor [tolerance=±5% resistance=470 package=THT]
  R8 = Resistor [tolerance=±5% resistance=470 package=THT]
  R9 = Resistor [tolerance=±5% resistance=470 package=THT]
  R10 = Resistor [tolerance=±5% resistance=470 package=THT]
  R11 = Resistor [tolerance=±5% resistance=470 package=THT]
  R12 = Resistor [tolerance=±5% resistance=470 package=THT]
  R13 = Resistor [tolerance=±5% resistance=470 package=THT]
  R14 = Resistor [tolerance=±5% resistance=470 package=THT]
  R15 = Resistor [tolerance=±5% resistance=470 package=THT]
  R16 = Resistor [tolerance=±5% resistance=470 package=THT]
  R17 = Resistor [tolerance=±5% resistance=470 package=THT]
  R18 = Resistor [tolerance=±5% resistance=470 package=THT]
  R19 = Resistor [tolerance=±5% resistance=470 package=THT]
  R20 = Resistor [tolerance=±5% resistance=470 package=THT]
  R21 = Resistor [tolerance=±5% resistance=470 package=THT]
  R22 = Resistor [tolerance=±5% resistance=470 package=THT]
  R23 = Resistor [tolerance=±5% resistance=470 package=THT]
  R24 = Resistor [tolerance=±5% resistance=470 package=THT]
  J1 = female pin header, 24 pins [form="♀ (female)"]
  U3 = 74HC595 [package="DIP16 [THT]"]
  U1 = 74HC595 [package="DIP16 [THT]"]
  U2 = 74HC595 [package="DIP16 [THT]"]
  Arduino1 = Arduino Mini (Rev5)

nets:
  N1: Part1.D8, U3.ST_CP, U1.ST_CP, U2.ST_CP
  N2: Part1.D11_PWM/MOSI, U1.DS
  N3: Part1.D13/SCK, U3.SH_CP, U1.SH_CP, U2.SH_CP
  GND: Part1.GND, U3.GND, U3.OE, U1.GND, U1.OE, U2.GND, U2.OE, Arduino1.GND
  5V: Part1.VIN, U3.MR, U3.VCC, U1.MR, U1.VCC, U2.MR, U2.VCC, Arduino1.5V
  N4: R1.Pin_0, U1.Q0
  N5: R1.Pin_1, J1.pin1
  N6: R2.Pin_0, U1.Q1
  N7: R2.Pin_1, J1.pin2
  N8: R3.Pin_0, U1.Q3
  N9: R3.Pin_1, J1.pin4
  N10: R4.Pin_0, U1.Q2
  N11: R4.Pin_1, J1.pin3
  N12: R5.Pin_0, U1.Q6
  N13: R5.Pin_1, J1.pin7
  N14: R6.Pin_0, U1.Q4
  N15: R6.Pin_1, J1.pin5
  N16: R7.Pin_0, U1.Q7
  N17: R7.Pin_1, J1.pin8
  N18: R8.Pin_0, U1.Q5
  N19: R8.Pin_1, J1.pin6
  N20: R9.Pin_0, U2.Q0
  N21: R9.Pin_1, J1.pin9
  N22: R10.Pin_0, U2.Q1
  N23: R10.Pin_1, J1.pin10
  N24: R11.Pin_0, U2.Q2
  N25: R11.Pin_1, J1.pin11
  N26: R12.Pin_0, U2.Q6
  N27: R12.Pin_1, J1.pin15
  N28: R13.Pin_0, U2.Q4
  N29: R13.Pin_1, J1.pin13
  N30: R14.Pin_0, U2.Q5
  N31: R14.Pin_1, J1.pin14
  N32: R15.Pin_0, U2.Q3
  N33: R15.Pin_1, J1.pin12
  N34: R16.Pin_0, U2.Q7
  N35: R16.Pin_1, J1.pin16
  N36: R17.Pin_0, U3.Q0
  N37: R17.Pin_1, J1.pin17
  N38: R18.Pin_0, U3.Q1
  N39: R18.Pin_1, J1.pin18
  N40: R19.Pin_0, U3.Q2
  N41: R19.Pin_1, J1.pin19
  N42: R20.Pin_0, U3.Q6
  N43: R20.Pin_1, J1.pin23
  N44: R21.Pin_0, U3.Q4
  N45: R21.Pin_1, J1.pin21
  N46: R22.Pin_0, U3.Q5
  N47: R22.Pin_1, J1.pin22
  N48: R23.Pin_0, U3.Q3
  N49: R23.Pin_1, J1.pin20
  N50: R24.Pin_0, U3.Q7
  N51: R24.Pin_1, J1.pin24
  N52: U3.DS, U2.Q7'
  N53: U1.Q7', U2.DS
